// Logisim project ALU_Main.circ as structural Verilog: 1 circuit, main circuit main
module main (
  input  [3:0] Input_A,
  input  [3:0] Input_B,
  input  [1:0] Opcode,
  output CarryBorrow,
  output [3:0] Result
);

  wire and_1_out;
  wire [3:0] adder_1_out, and_2_out, bit_extender_1_out, or_1_out, xor_1_out;

  and and_1 (and_1_out, Opcode[0], Opcode[1]);
  assign bit_extender_1_out = {{3{and_1_out}}, and_1_out};  // Bit_Extender bit_extender_1
  assign xor_1_out = bit_extender_1_out ^ Input_B;  // XOR_Gate xor_1, 4 bits wide
  Adder #(.width(4)) adder_1 (.a(Input_A), .b(xor_1_out), .out(adder_1_out), .cin(and_1_out), .cout(CarryBorrow));
  assign and_2_out = Input_A & Input_B;  // AND_Gate and_2, 4 bits wide
  assign or_1_out = Input_A | Input_B;  // OR_Gate or_1, 4 bits wide
  Multiplexer #(.select(2), .width(4)) multiplexer_1 (
    .in0(and_2_out), .in1(or_1_out), .in2(adder_1_out), .in3(adder_1_out), .out(Result), .sel(Opcode));

  // Notes on the sheet:
  //   00=AND
  //   01=OR
  //   10=ADD
  //   11=SUB
  //   SUB_ACTIVE
  //   4-Bit ALU
  //   with 4 Operations: AND, OR, ADD, SUB
  //   Team Members:
  //   Youssef Sameh
  //   Dalia Mohamed
  //   Malak Mohamed
  //   Innovation University, Egypt
  //   GITHUB: yecreate
endmodule
