// Logisim project Discrete_Mux.circ as structural Verilog: 1 circuit, main circuit main
module main (
);

  wire Bit_2_Inputs_sw4, Bit_3_Inputs_sw2, Bit_3_Inputs_sw3, Bit_3_Inputs_sw4, n7404_1_pin1, n7404_1_pin2,
       n7404_1_pin3, n7404_1_pin4, n7411_1_pin2, n7411_1_pin5, n7411_1_pin6, n7411_1_pin8, n7411_1_pin11,
       n7411_1_pin12, n7411_2_pin4, n7411_2_pin6, n7432_1_pin3, n7432_1_pin6, n7432_1_pin8, n7432_1_pin10,
       n7432_2_pin2, n7432_2_pin3, n7432_2_pin5, n7432_2_pin6, n7432_2_pin8, n7432_2_pin10;

  _7404 #(.ShowInternalStructure("true")) u_7404_1 (
    .pin1(n7404_1_pin1), .pin2(n7404_1_pin2), .pin3(n7404_1_pin3), .pin4(n7404_1_pin4));  // open: pin5, pin6, pin13, pin12, pin11, pin10, pin9, pin8
  DipSwitch #(.number(2)) SEL (.sw1(n7404_1_pin1), .sw2(n7404_1_pin3));
  _7411 #(.ShowInternalStructure("true")) u_7411_1 (
    .pin1(n7404_1_pin4), .pin2(n7411_1_pin2), .pin3(n7404_1_pin2), .pin4(n7404_1_pin3), .pin5(n7411_1_pin5),
    .pin6(n7411_1_pin6), .pin13(n7404_1_pin2), .pin12(n7411_1_pin12), .pin11(n7411_1_pin11),
    .pin10(n7404_1_pin4), .pin9(n7404_1_pin1), .pin8(n7411_1_pin8));
  DipSwitch #(.number(4)) Bit_2_Inputs (
    .sw1(n7411_1_pin2), .sw2(n7411_1_pin5), .sw3(n7411_1_pin11), .sw4(Bit_2_Inputs_sw4));
  _7432 #(.ShowInternalStructure("true")) u_7432_1 (
    .pin1(n7411_1_pin12), .pin2(n7411_1_pin6), .pin3(n7432_1_pin3), .pin4(n7432_1_pin3), .pin5(n7411_1_pin8),
    .pin6(n7432_1_pin6), .pin10(n7432_1_pin10), .pin9(n7432_1_pin6), .pin8(n7432_1_pin8));  // open: pin13, pin12, pin11
  LED Q2 (.in(n7432_1_pin8));
  _7411 #(.ShowInternalStructure("true")) u_7411_2 (
    .pin1(n7404_1_pin3), .pin2(Bit_2_Inputs_sw4), .pin3(n7404_1_pin2), .pin4(n7411_2_pin4),
    .pin5(n7404_1_pin4), .pin6(n7411_2_pin6), .pin13(n7404_1_pin1), .pin12(n7432_1_pin10));  // open: pin11, pin10, pin9, pin8
  _7432 #(.ShowInternalStructure("true")) u_7432_2 (
    .pin1(n7411_2_pin6), .pin2(n7432_2_pin2), .pin3(n7432_2_pin3), .pin4(n7432_2_pin3), .pin5(n7432_2_pin5),
    .pin6(n7432_2_pin6), .pin10(n7432_2_pin10), .pin9(n7432_2_pin6), .pin8(n7432_2_pin8));  // open: pin13, pin12, pin11
  DipSwitch #(.number(4)) Bit_3_Inputs (
    .sw1(n7411_2_pin4), .sw2(Bit_3_Inputs_sw2), .sw3(Bit_3_Inputs_sw3), .sw4(Bit_3_Inputs_sw4));
  LED Q3 (.in(n7432_2_pin8));
  _7411 #(.ShowInternalStructure("true")) u_7411_3 (
    .pin1(n7404_1_pin3), .pin2(Bit_3_Inputs_sw2), .pin3(n7404_1_pin1), .pin4(n7404_1_pin4),
    .pin5(Bit_3_Inputs_sw3), .pin6(n7432_2_pin5), .pin13(n7404_1_pin2), .pin12(n7432_2_pin2),
    .pin11(Bit_3_Inputs_sw4), .pin10(n7404_1_pin3), .pin9(n7404_1_pin1), .pin8(n7432_2_pin10));

  // Notes on the sheet:
  //   GITHUB: yecreate
  //   Team Members:
  //   Components:
  //   1x 7404
  //   3x 7411
  //   2x 7432
  //   7404
  //   74HC153 Alternative
  //   Dual 4:1 MUX with 2-Select
  //   Innovation University, Egypt
  //   Youssef Sameh
  //   Dalia Mohamed
  //   Malak Mohamed
  //   7411
  //   7432
  //   D0/D1/D2/D3
  //   7411
  //   OUTPUTS
  //   7432
  //   7411
  //   D0/D1/D2/D3
endmodule
